# Fritzing sketch trover_mod (saved by Fritzing 0.9.4)
breadboards: 1

parts:
  Part1 = Arduino Uno (Rev3)
  Part2 = Thumb Joystick
  IC1 = IC, DIP package, 14 pins [chip_label="MCP 4241"]
  S1 = Toggle Switch [package=THT]  # not connected
  J1 = JST-B3P-VH [part_number=JST-B3P-VH package=THT]
  J2 = JST-B3P-VH [part_number=JST-B3P-VH package=THT]
  LED1 = DUO LED RG [package="5 mm [THT]"]  # not connected
  R1 = Rotary Potentiometer (Small) [maximum_resistance=100kΩ package=THT]  # not connected
  R2 = Rotary Potentiometer (Small) [maximum_resistance=100kΩ package=THT]  # not connected
  R3 = Rotary Potentiometer (Small) [maximum_resistance=100kΩ package=THT]  # not connected
  R4 = Rotary Potentiometer (Small) [maximum_resistance=100kΩ package=THT]  # not connected
  S2 = Toggle Switch [package=THT]  # not connected

nets:
  N1: Part1.A0, IC1.pin6, J1.pin2
  N2: Part1.A1, Part2.HORZ
  N3: Part1.A2, Part2.VERT
  N4: Part1.D10_PWM/SS, IC1.pin1
  N5: Part1.D11_PWM/MOSI, IC1.pin3
  N6: Part1.D13/SCK, IC1.pin2
  N7: Part1.D2, Part2.SEL
  N8: Part1.3V3, IC1.pin14
  5V: Part1.5V, Part2.VCC
  GND: Part1.GND, Part2.GND
  N9: IC1.pin5, J1.pin3
  N10: IC1.pin7, J1.pin1
  N11: IC1.pin9, J2.pin3
  N12: IC1.pin10, J2.pin2
  N13: IC1.pin11, J2.pin1
